# Fritzing sketch vdscroller (saved by Fritzing 0.9.3b)
perfboards: 1

parts:
  Part1 = Adafruit Micro USB Breakout [part_number="Adafruit #1833"]
  Part2 = Adafruit Switched JST Breakout [part_number="Adafruit #1863"]
  LIPO = SOT23-6 TO DIP [package="SOT23-6 TO DIP"]
  MOSKY = SOT23-6 TO DIP [package="SOT23-6 TO DIP"]
  3_3V = SOT23-6 TO DIP [package="SOT23-6 TO DIP"]
  J1 = female pin header, 8 pins [form="♀ (female)"]
  J2 = female pin header, 8 pins [form="♀ (female)"]
  C2 = Electrolytic Capacitor [capacitance=4.7µF package="100 mil [THT, electrolytic]"]
  C3 = Electrolytic Capacitor [capacitance=4.7µF package="100 mil [THT, electrolytic]"]
  C4 = Electrolytic Capacitor [capacitance=4.7µF package="100 mil [THT, electrolytic]"]
  LED2 = LED - 5mm [color="Green (555nm)" package="5 mm [THT]"]
  LED1 = LED - 5mm [color="Red (633nm)" package="5 mm [THT]"]
  R8 = Resistor [tolerance=±5% resistance=470 package=THT]
  R7 = Resistor [tolerance=±5% resistance=470 package=THT]
  R9 = Resistor [tolerance=±5% resistance=2k package=THT]
  R10 = Resistor [tolerance=±5% resistance=100k package=THT]
  R11 = Resistor [tolerance=±5% resistance=10k package=THT]
  C5 = Electrolytic Capacitor [capacitance=4.7µF package="100 mil [THT, electrolytic]"]
  R12 = Resistor [tolerance=±5% resistance=10k package=THT]
  R13 = Resistor [tolerance=±5% resistance=10k package=THT]
  R14 = Resistor [tolerance=±5% resistance=10k package=THT]
  R15 = Resistor [tolerance=±5% resistance=10k package=THT]
  R16 = Resistor [tolerance=±5% resistance=10k package=THT]
  R17 = Resistor [tolerance=±5% resistance=10k package=THT]
  R18 = Resistor [tolerance=±5% resistance=2.2k package=THT]

nets:
  GND: Part1.GND, Part2.GND, LIPO.VSS, C2.-, C4.-, LED2.cathode, R9.Pin_0, R10.Pin_0, C5.-
  N1: Part1.VBUS, MOSKY.VDD, MOSKY.VOUT, C4.+, LED1.anode, R10.Pin_1
  N2: Part2.V+, LIPO.VOUT, MOSKY.AO, C2.+
  N3: LIPO.VDD, R8.Pin_1, R7.Pin_1
  N4: LIPO.SDA, R9.Pin_1
  VSS: MOSKY.VSS, MOSKY.SDA, 3_3V.VDD, C3.+, R11.Pin_1
  N5: 3_3V.VSS, C3.-
  N6: 3_3V.VOUT, R11.Pin_0
  N7: 3_3V.SCL, J1.pin8, C5.+, R12.Pin_0, R13.Pin_0, R15.Pin_1, R16.Pin_1
  N8: J1.pin1, R13.Pin_1
  N9: J1.pin3, R12.Pin_1
  N10: J2.pin5, R16.Pin_0
  N11: J2.pin6, R15.Pin_0
  N12: J2.pin7, R14.Pin_0
  N13: J2.pin8, R14.Pin_1
  N14: LED2.anode, R8.Pin_0
  N15: LED1.cathode, R7.Pin_0
  N16: R17.Pin_1, R18.Pin_0

custom parts:
  Adafruit Micro USB Breakout: Simple but effective - this breakout board has a USB Micro-B connector, with all 5 pins broken out. Great for pairing with a microcontroller with USB support, or adding USB 5V power to a project. We use a micro-AB connector with through-hole shielding pads for an excellent strong connection - it won't rip off by accident! Comes with one fully assembled and tested micro B breakout PCB and a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
  Adafruit Switched JST Breakout: This switched JST connector is the best way to quickly prototype with our LiPoly batteries. We paired a genuine JST connector with a slide switch that can do up to 600mA. Both are soldered onto a breadboard-friendly breakout. There's two ground pins, one 'switched' power pin, and one pin that is always on. This is compatible with the "JST PH 2-pin" connectors we use in our battery packs..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
