# Fritzing sketch vdscroller2 (saved by Fritzing 0.9.3b)
perfboards: 2

parts:
  Part1 = Adafruit Micro USB Breakout [part_number="Adafruit #1833"]
  Part2 = Adafruit Switched JST Breakout [part_number="Adafruit #1863"]
  LIPO = SOT23-6 TO DIP [package="SOT23-6 TO DIP"]
  MOSKY = SOT23-6 TO DIP [package="SOT23-6 TO DIP"]
  3_3V = SOT23-6 TO DIP [package="SOT23-6 TO DIP"]  # not connected
  C2 = Electrolytic Capacitor [capacitance=4.7µF package="100 mil [THT, electrolytic]"]  # not connected
  C3 = Electrolytic Capacitor [capacitance=4.7µF voltage=6.3V package="100 mil [THT, electrolytic]"]  # not connected
  C4 = Electrolytic Capacitor [capacitance=100nF package="100 mil [THT, electrolytic]"]
  R8 = Resistor [tolerance=±5% resistance=470 package=THT]
  R7 = Resistor [tolerance=±5% resistance=470 package=THT]
  R9 = Resistor [tolerance=±5% resistance=2k package=THT]
  R10 = Resistor [tolerance=±5% resistance=100k package=THT]
  R11 = Resistor [tolerance=±5% resistance=10k package=THT]  # not connected
  C5 = Electrolytic Capacitor [capacitance=4.7µF package="100 mil [THT, electrolytic]"]
  LED3 = LED - 3mm [color="Red (633nm)" package="3 mm [THT]"]
  LED2 = LED - 3mm [color="Green (555nm)" package="3 mm [THT]"]
  R12 = Resistor [tolerance=±5% resistance=10k package=THT]  # not connected
  R13 = Resistor [tolerance=±5% resistance=10k package=THT]  # not connected
  R14 = Resistor [tolerance=±5% resistance=10k package=THT]  # not connected
  R15 = Resistor [tolerance=±5% resistance=10k package=THT]  # not connected
  R16 = Resistor [tolerance=±5% resistance=10k package=THT]  # not connected
  R17 = Resistor [tolerance=±5% resistance=10k package=THT]  # not connected
  R18 = Resistor [tolerance=±5% resistance=2.2k package=THT]  # not connected
  Adafruit_HUZZAH_ESP8266_Breakout1 = Adafruit HUZZAH ESP8266 Breakout [part_number=2471]  # not connected
  J1 = male pin header, 10 pins [form="♂ (male)"]  # not connected
  J2 = male pin header, 10 pins [form="♂ (male)"]  # not connected

nets (from the breadboard view):
  N1: Part1.GND, R9.Pin_1
  N2: Part1.VBUS, LIPO.AO, MOSKY.VDD, MOSKY.VOUT, C4.+, R10.Pin_0, LED3.anode
  N3: Part2.GND, C5.-
  N4: LIPO.VDD, R8.Pin_0, R7.Pin_0
  N5: LIPO.VSS, C4.-, R10.Pin_1, LED2.anode
  N6: LIPO.VOUT, MOSKY.AO
  N7: LIPO.SDA, R9.Pin_0
  N8: MOSKY.VSS, MOSKY.SDA

notes:
  ESP on back (mirror pins)

custom parts:
  Adafruit Micro USB Breakout: Simple but effective - this breakout board has a USB Micro-B connector, with all 5 pins broken out. Great for pairing with a microcontroller with USB support, or adding USB 5V power to a project. We use a micro-AB connector with through-hole shielding pads for an excellent strong connection - it won't rip off by accident! Comes with one fully assembled and tested micro B breakout PCB and a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
  Adafruit Switched JST Breakout: This switched JST connector is the best way to quickly prototype with our LiPoly batteries. We paired a genuine JST connector with a slide switch that can do up to 600mA. Both are soldered onto a breadboard-friendly breakout. There's two ground pins, one 'switched' power pin, and one pin that is always on. This is compatible with the "JST PH 2-pin" connectors we use in our battery packs..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
